// Logisim project GREGS.circ as structural Verilog: 1 circuit, main circuit GREGS
module GREGS (
  input  [15:0] Z,
  input  L_A_HI,
  input  n_EL_A,
  input  L_A_LO,
  input  L_B_HI,
  input  n_EL_B,
  input  L_B_LO,
  input  nEL_C,
  input  L_C,
  input  nEL_DP,
  input  L_DP,
  input  nEL_SP,
  input  L_SP,
  input  nEL_SSP,
  input  L_SSP,
  input  nEL_PC,
  input  L_PC,
  input  nEL_TPC,
  input  COMMIT,
  output [15:0] L
);

  wire [7:0] A_HI_q, A_LO_q, B_HI_q, B_LO_q;
  wire [15:0] C_q, DP_q, PC_q, SP_q, SSP_q, TPC_q;

  Register A_HI (.D(Z[7:0]), .en(1'b1), .clk(L_A_HI), .Q(A_HI_q));  // open: clr
  Register A_LO (.D(Z[15:8]), .en(1'b1), .clk(L_A_LO), .Q(A_LO_q));  // open: clr
  Register B_HI (.D(Z[7:0]), .en(1'b1), .clk(L_B_HI), .Q(B_HI_q));  // open: clr
  Register B_LO (.D(Z[15:8]), .en(1'b1), .clk(L_B_LO), .Q(B_LO_q));  // open: clr
  Register #(.width(16)) C (.D(Z), .en(1'b1), .clk(L_C), .Q(C_q));  // open: clr
  Register #(.width(16)) DP (.D(Z), .en(1'b1), .clk(L_DP), .Q(DP_q));  // open: clr
  Register #(.width(16)) SP (.D(Z), .en(1'b1), .clk(L_SP), .Q(SP_q));  // open: clr
  Register #(.width(16)) SSP (.D(Z), .en(1'b1), .clk(L_SSP), .Q(SSP_q));  // open: clr
  Register #(.width(16)) PC (.D(Z), .en(1'b1), .clk(L_PC), .Q(PC_q));  // open: clr
  Register #(.width(16)) TPC (.D(L), .en(1'b1), .clk(COMMIT), .Q(TPC_q));  // open: clr
  assign L[7:0] = n_EL_A ? A_HI_q : 8'bz;  // Controlled_Buffer controlled_buffer_1
  assign L[15:8] = n_EL_A ? A_LO_q : 8'bz;  // Controlled_Buffer controlled_buffer_2
  assign L[7:0] = n_EL_B ? B_HI_q : 8'bz;  // Controlled_Buffer controlled_buffer_3
  assign L[15:8] = n_EL_B ? B_LO_q : 8'bz;  // Controlled_Buffer controlled_buffer_4
  assign L = nEL_C ? C_q : 16'bz;  // Controlled_Buffer controlled_buffer_5
  assign L = nEL_DP ? DP_q : 16'bz;  // Controlled_Buffer controlled_buffer_6
  assign L = nEL_SP ? SP_q : 16'bz;  // Controlled_Buffer controlled_buffer_7
  assign L = nEL_SSP ? SSP_q : 16'bz;  // Controlled_Buffer controlled_buffer_8
  assign L = nEL_PC ? PC_q : 16'bz;  // Controlled_Buffer controlled_buffer_9
  assign L = nEL_TPC ? TPC_q : 16'bz;  // Controlled_Buffer controlled_buffer_10
endmodule
