// Logisim project IR_DECODE.circ as structural Verilog: 1 circuit, main circuit IR_DECODE
module IR_DECODE (
  input  [15:0] L_INPUT,
  input  [15:0] R,
  input  nFP_WRITE,
  input  [1:0] CLOCK_SELECT,
  input  MANUAL_CLK,
  input  nBP_RESET,
  input  [7:0] DBUS,
  input  [3:0] FP_L,
  input  nSTOP_CLK,
  input  nDMA_REQ,
  input  [5:0] nIRQ,
  input  [15:0] MAR,
  output [7:0] IR,
  output [15:0] L_INT,
  output INIT_INST,
  output IOCLK,
  output nDMA_ACK,
  output nRESET,
  output [6:0] XL_CTLBUS,
  output CLKS,
  output [15:0] Z,
  output nHALT,
  output [7:0] MSW_FLAGS,
  output [1:0] nER_CTLBUS,
  output [11:0] nEL_CTLBUS,
  output [15:0] L_MSW,
  output XINIT_INST,
  output [15:0] T,
  output [20:0] L_CTLBUS,
  output nWAIT,
  output MEMREF,
  output nNW,
  output nNP,
  output [21:0] A,
  output nWR,
  output [1:0] IMMVAL,
  output MEMORY,
  output nRW
);

  wire alu_1_aluc, alu_1_alus, alu_1_aluv, alu_1_aluz, clocks_1_clkm, faults_int_1_fault_pending,
       faults_int_1_rl_fault, field_decode_1_ndo_branch, field_decode_1_ndo_rshift, field_decode_1_ne_pte,
       field_decode_1_nset_flags, field_decode_1_r_l_pte, field_decode_1_rcommit, field_decode_1_rl_a_hi,
       field_decode_1_rl_a_lo, field_decode_1_rl_b_hi, field_decode_1_rl_b_lo, field_decode_1_rl_c,
       field_decode_1_rl_dp, field_decode_1_rl_fpl, field_decode_1_rl_ie, field_decode_1_rl_mdr,
       field_decode_1_rl_msw, field_decode_1_rl_pc, field_decode_1_rl_ptb, field_decode_1_rl_sp,
       field_decode_1_rl_ssp, field_decode_2_1_nclks, microcode_1_aluop_sz, microcode_1_code_ptb,
       microcode_1_latch_sz, microcode_1_r_rw, microcode_1_ruser_ptb, microcode_1_use_carry,
       page_table_1_xcode_ptb;
  wire [1:0] microcode_1_alu_op, microcode_1_er, microcode_1_rimm_val;
  wire [3:0] faults_int_1_encoder, microcode_1_el, microcode_1_latch, microcode_1_misc;
  wire [5:0] field_decode_1_nbkpt;
  wire [15:0] alu_1_q;

  CLOCKS clocks_1 (
    .nHALT(nHALT), .CLOCK_SELECT(CLOCK_SELECT), .MANUAL_CLK(MANUAL_CLK), .nWAIT(nWAIT),
    .nSTOP_CLK(nSTOP_CLK), .nBP_RESET(nBP_RESET), .IOCLK(IOCLK), .CLKM(clocks_1_clkm), .CLKS(CLKS),
    .nRESET(nRESET));
  FAULTS_INT faults_int_1 (
    .nNP(nNP), .MSWM(MSW_FLAGS[3]), .nNW(nNW), .nBKPT(field_decode_1_nbkpt[0]),
    .PRIV(field_decode_1_nbkpt[1]), .MSWV(MSW_FLAGS[4]), .nTRAPO(field_decode_1_nbkpt[2]),
    .nSYSCALL(field_decode_1_nbkpt[3]), .CLKM(clocks_1_clkm), .nDMA_REQ(nDMA_REQ), .MSWE(MSW_FLAGS[1]),
    .nNEXT0(field_decode_1_nbkpt[4]), .CLKS(CLKS), .nCLR_TRAP(field_decode_1_nbkpt[5]), .nIRQ0(nIRQ[0]),
    .nRESET(nRESET), .IOCLK(IOCLK), .nIRQ1(nIRQ[1]), .nEL_FCODE(nEL_CTLBUS[11]), .nIRQ2(nIRQ[2]),
    .nIRQ3(nIRQ[3]), .nIRQ4(nIRQ[4]), .nIRQ5(nIRQ[5]), .FAULT_PENDING(faults_int_1_fault_pending),
    .ENCODER(faults_int_1_encoder), .RL_FAULT(faults_int_1_rl_fault), .L(L_INT));
  Field_Decode field_decode_1 (
    .RL_C(field_decode_1_rl_c), .RL_PC(field_decode_1_rl_pc), .RL_DP(field_decode_1_rl_dp),
    .RL_SP(field_decode_1_rl_sp), .RL_A_LO(field_decode_1_rl_a_lo), .RL_B_LO(field_decode_1_rl_b_lo),
    .RL_SSP(field_decode_1_rl_ssp), .RL_A_HI(field_decode_1_rl_a_hi), .RL_B_HI(field_decode_1_rl_b_hi),
    .nEL_MDR(nEL_CTLBUS[1]), .nEL_SSP(nEL_CTLBUS[3]), .nEL_TPC(nEL_CTLBUS[5]), .nEL_FCODE(nEL_CTLBUS[11]),
    .nEL_MAR(nEL_CTLBUS[0]), .nEL_MSW(nEL_CTLBUS[2]), .nEL_C(nEL_CTLBUS[4]), .nEL_PC(nEL_CTLBUS[6]),
    .nEL_DP(nEL_CTLBUS[9]), .nEL_SP(nEL_CTLBUS[10]), .nEL_A(nEL_CTLBUS[7]), .nEL_B(nEL_CTLBUS[8]),
    .nDO_RSHIFT(field_decode_1_ndo_rshift), .nDMA_ACK(nDMA_ACK), .nDO_BRANCH(field_decode_1_ndo_branch),
    .nSYSCALL(field_decode_1_nbkpt[3]), .nHALT(nHALT), .nBKPT(field_decode_1_nbkpt[0]),
    .nTRAPO(field_decode_1_nbkpt[2]), .nE_PTE(field_decode_1_ne_pte), .nSET_FLAGS(field_decode_1_nset_flags),
    .INIT_INST(INIT_INST), .RL_IE(field_decode_1_rl_ie), .nCLR_TRAP(field_decode_1_nbkpt[5]),
    .R_L_PTE(field_decode_1_r_l_pte), .XINIT_INST(XINIT_INST), .RCOMMIT(field_decode_1_rcommit),
    .RL_MSW(field_decode_1_rl_msw), .RL_MDR(field_decode_1_rl_mdr), .RL_PTB(field_decode_1_rl_ptb),
    .RL_FPL(field_decode_1_rl_fpl), .nER_MDR(nER_CTLBUS[1]), .nER_IMM(nER_CTLBUS[0]),
    .LATCH(microcode_1_latch), .FP_L(FP_L), .nSTOP_CLK(nSTOP_CLK), .IR(IR), .EL(microcode_1_el),
    .MISC(microcode_1_misc), .FAULT_PENDING(faults_int_1_fault_pending), .nCLKS(field_decode_2_1_nclks),
    .MSWM(MSW_FLAGS[3]), .LATCH_SZ(microcode_1_latch_sz), .ER(microcode_1_er));
  Field_Decode_2 field_decode_2_1 (
    .COMMIT(L_CTLBUS[5]), .L_FPL(L_CTLBUS[6]), .L_PTB(L_CTLBUS[7]), .L_A_HI(L_CTLBUS[8]),
    .L_B_HI(L_CTLBUS[9]), .L_SSP(L_CTLBUS[10]), .L_C(L_CTLBUS[11]), .L_PC(L_CTLBUS[12]), .L_DP(L_CTLBUS[13]),
    .L_SP(L_CTLBUS[14]), .L_A_LO(L_CTLBUS[15]), .L_B_LO(L_CTLBUS[16]), .L_MSW(L_CTLBUS[17]),
    .L_IE(L_CTLBUS[18]), .nL_PTE(L_CTLBUS[19]), .L_FAULT(L_CTLBUS[20]), .IMMVAL(IMMVAL),
    .nCLKS(field_decode_2_1_nclks), .L_MODE(L_CTLBUS[0]), .L_PAGING(L_CTLBUS[1]), .L_MDR_LO(L_CTLBUS[2]),
    .L_MDR_HI(L_CTLBUS[3]), .L_MAR(L_CTLBUS[4]), .nWR(nWR), .nRW(nRW), .RCOMMIT(field_decode_1_rcommit),
    .RL_FPL(field_decode_1_rl_fpl), .RL_PTB(field_decode_1_rl_ptb), .RL_A_HI(field_decode_1_rl_a_hi),
    .RL_B_HI(field_decode_1_rl_b_hi), .RL_SSP(field_decode_1_rl_ssp), .RL_C(field_decode_1_rl_c),
    .RL_PC(field_decode_1_rl_pc), .RL_DP(field_decode_1_rl_dp), .RL_SP(field_decode_1_rl_sp),
    .RL_A_LO(field_decode_1_rl_a_lo), .RL_B_LO(field_decode_1_rl_b_lo), .RL_MSW(field_decode_1_rl_msw),
    .RL_IE(field_decode_1_rl_ie), .R_L_PTE(field_decode_1_r_l_pte), .RL_FAULT(faults_int_1_rl_fault),
    .RIMMVAL(microcode_1_rimm_val), .CLKS(CLKS), .XL_MODE(XL_CTLBUS[3]), .XL_PAGING(XL_CTLBUS[4]),
    .XL_MDR_LO(XL_CTLBUS[1]), .XL_MDR_HI(XL_CTLBUS[2]), .RL_MDR(field_decode_1_rl_mdr),
    .XL_MAR(XL_CTLBUS[0]), .R_RW(microcode_1_r_rw), .FAULT_PENDING(faults_int_1_fault_pending));
  Microcode microcode_1 (
    .nNEXT0(field_decode_1_nbkpt[4]), .EL(microcode_1_el), .ER(microcode_1_er),
    .RIMM_VAL(microcode_1_rimm_val), .ALUOP_SZ(microcode_1_aluop_sz), .ALU_OP(microcode_1_alu_op),
    .USE_CARRY(microcode_1_use_carry), .LATCH_SZ(microcode_1_latch_sz), .RUSER_PTB(microcode_1_ruser_ptb),
    .CODE_PTB(microcode_1_code_ptb), .LATCH(microcode_1_latch), .XL_MAR(XL_CTLBUS[0]),
    .XL_MDR_LO(XL_CTLBUS[1]), .XL_MDR_HI(XL_CTLBUS[2]), .PRIV(field_decode_1_nbkpt[1]),
    .XL_MODE(XL_CTLBUS[3]), .XL_PAGING(XL_CTLBUS[4]), .MISC(microcode_1_misc), .nE_MDR_LO(XL_CTLBUS[6]),
    .nE_MDR_HI(XL_CTLBUS[5]), .R_RW(microcode_1_r_rw), .IR(IR), .CLK_M(clocks_1_clkm), .nRESET(nRESET),
    .MSWC(MSW_FLAGS[6]), .MSWZ(MSW_FLAGS[7]), .MSWS(MSW_FLAGS[5]), .MSWV(MSW_FLAGS[4]),
    .nFP_WRITE(nFP_WRITE), .nDMA_ACQ(nDMA_ACK), .DBUS(DBUS), .INIT_INST(INIT_INST),
    .ENCODER(faults_int_1_encoder), .FAULT_PENDING(faults_int_1_fault_pending),
    .nDO_BRANCH(field_decode_1_ndo_branch));
  ALU alu_1 (
    .Z(Z), .ALUV(alu_1_aluv), .ALUC(alu_1_aluc), .ALUS(alu_1_alus), .ALUZ(alu_1_aluz), .Q(alu_1_q),
    .nDO_RSHIFT(field_decode_1_ndo_rshift), .ALUOP_SZ(microcode_1_aluop_sz), .IR(IR),
    .ALU_OP(microcode_1_alu_op), .USE_CARRY(microcode_1_use_carry), .MSWC(MSW_FLAGS[6]), .L(L_INPUT), .R(R));
  // NoConnect on alu_1_q
  MSW msw_1 (
    .MSWV(MSW_FLAGS[4]), .MSWZ(MSW_FLAGS[7]), .MSWC(MSW_FLAGS[6]), .MSWS(MSW_FLAGS[5]), .MSWM(MSW_FLAGS[3]),
    .L(L_MSW), .MSWE(MSW_FLAGS[1]), .MSWP(MSW_FLAGS[0]), .Z(Z), .L_FAULT(L_CTLBUS[20]), .MEMREF(MEMREF),
    .xCODE_PTB(page_table_1_xcode_ptb), .L_EI(L_CTLBUS[18]), .nRESET(nRESET), .L_PAGING(L_CTLBUS[1]),
    .L_MODE(L_CTLBUS[0]), .nEL_MSW(nEL_CTLBUS[2]), .ALUS(alu_1_alus), .ALUC(alu_1_aluc), .ALUZ(alu_1_aluz),
    .ALUV(alu_1_aluv), .nSET_FLAGS(field_decode_1_nset_flags), .L_MSW(L_CTLBUS[17]));
  PAGE_TABLE page_table_1 (
    .MAR(MAR), .nRESET(nRESET), .L_PTB(L_CTLBUS[7]), .L_BUS(L_INPUT), .nL_PTE(L_CTLBUS[19]),
    .nE_PTE(field_decode_1_ne_pte), .MSWM(MSW_FLAGS[3]), .MSWP(MSW_FLAGS[0]),
    .USER_PTB(microcode_1_ruser_ptb), .CODE_PTB(microcode_1_code_ptb), .L_MAR(L_CTLBUS[4]), .nRW(nRW),
    .XINIT_INST(XINIT_INST), .XL_MDR_LO(XL_CTLBUS[1]), .XL_MDR_HI(XL_CTLBUS[2]), .nE_MDR_LO(XL_CTLBUS[6]),
    .nE_MDR_HI(XL_CTLBUS[5]), .CLKM(clocks_1_clkm), .nDMA_ACK(nDMA_ACK), .T(T), .nWAIT(nWAIT),
    .MEMREF(MEMREF), .nNW(nNW), .xCODE_PTB(page_table_1_xcode_ptb), .nNP(nNP), .A_BUS(A), .MEMORY(MEMORY));  // open: xMSWM, xUSER_PTB, xMSWP, F, M, W, P

  assign MSW_FLAGS[2] = 1'b0;

  // Notes on the sheet:
  //   nINT_CTL
endmodule
