// Logisim project MDR.circ as structural Verilog: 1 circuit, main circuit MDR
module MDR (
  input  XL_MDR_HIGH,
  input  XL_MDR_LOW,
  input  [15:0] Z,
  input  nDMA_ACK,
  input  nRW,
  input  nE_MDR_HIGH,
  input  L_MDR_HIGH,
  input  nEL_MDR,
  input  nER_MDR,
  input  L_MDR_LOW,
  input  COMMIT,
  input  nE_MDR_LOW,
  output [7:0] D,
  output [7:0] DBUS,
  output [15:0] L,
  output [15:0] R,
  output [15:0] T
);

  wire not_1_out, not_2_out, not_3_out, not_4_out, U51_y1, U51_y2, U51_y3, U51_y4, U52_y1, U52_y2, U52_y3,
       U52_y4, U62_y1, U62_y2, U63_y1, U63_y2, U64_y1, U64_y2, U65_y1, U65_y2;

  not not_1 (not_1_out, nDMA_ACK);
  SN74245 U61 (.nG(not_1_out), .DIR(nRW), .A(D), .B(DBUS));
  IC_74153 U65 (
    .Y1(U65_y1), .Y2(U65_y2), .C1(1'b0), .D1(D[0]), .A2(Z[1]), .A1(Z[0]), .B2(D[1]), .C2(1'b0), .D2(D[0]),
    .S0(XL_MDR_HIGH), .S1(XL_MDR_LOW), .OE1(1'b0), .OE2(1'b0), .B1(D[0]));
  IC_74153 U64 (
    .Y1(U64_y1), .Y2(U64_y2), .C1(1'b0), .D1(D[0]), .A2(Z[3]), .A1(Z[2]), .B2(D[3]), .C2(1'b0), .D2(D[0]),
    .S0(XL_MDR_HIGH), .S1(XL_MDR_LOW), .OE1(1'b0), .OE2(1'b0), .B1(D[2]));
  IC_74153 U63 (
    .Y1(U63_y1), .Y2(U63_y2), .C1(1'b0), .D1(D[0]), .A2(Z[5]), .A1(Z[4]), .B2(D[5]), .C2(1'b0), .D2(D[0]),
    .S0(XL_MDR_HIGH), .S1(XL_MDR_LOW), .OE1(1'b0), .OE2(1'b0), .B1(D[4]));
  IC_74153 U62 (
    .Y1(U62_y1), .Y2(U62_y2), .C1(1'b0), .D1(D[0]), .A2(Z[7]), .A1(Z[6]), .B2(D[7]), .C2(1'b0), .D2(D[0]),
    .S0(XL_MDR_HIGH), .S1(XL_MDR_LOW), .OE1(1'b0), .OE2(1'b0), .B1(D[6]));
  IC_74157 U52 (
    .Y2(U52_y2), .Y3(U52_y3), .Y4(U52_y4), .Y1(U52_y1), .A2(Z[9]), .B2(D[1]), .A3(Z[10]), .B3(D[2]),
    .A4(Z[11]), .A1(Z[8]), .B4(D[3]), .S0(XL_MDR_LOW), .OE(1'b0), .B1(D[0]));
  IC_74157 U51 (
    .Y2(U51_y2), .Y3(U51_y3), .Y4(U51_y4), .Y1(U51_y1), .A2(Z[13]), .B2(D[5]), .A3(Z[14]), .B3(D[6]),
    .A4(Z[15]), .A1(Z[12]), .B4(D[7]), .S0(XL_MDR_LOW), .OE(1'b0), .B1(D[4]));
  not not_2 (not_2_out, COMMIT);
  IC_74273 U54 (
    .Y2(T[1]), .Y3(T[2]), .Y1(T[0]), .Y4(T[3]), .Y5(T[4]), .Y6(T[5]), .Y7(T[6]), .Y8(T[7]), .D2(U65_y2),
    .D3(U64_y1), .D1(U65_y1), .D4(U64_y2), .D5(U63_y1), .D6(U63_y2), .D7(U62_y1), .D8(U62_y2),
    .CLK(L_MDR_HIGH), .CLR(not_2_out));
  IC_74273 U53 (
    .Y2(T[9]), .Y3(T[10]), .Y1(T[8]), .Y4(T[11]), .Y5(T[12]), .Y6(T[13]), .Y7(T[14]), .Y8(T[15]),
    .D2(U52_y2), .D3(U52_y3), .D1(U52_y1), .D4(U52_y4), .D5(U51_y1), .D6(U51_y2), .D7(U51_y3), .D8(U51_y4),
    .CLK(L_MDR_LOW), .CLR(not_2_out));
  IC_74244 ic_74244_1 (
    .Y3(D[2]), .Y4(D[3]), .Z1(D[4]), .Y1(D[0]), .Z2(D[5]), .Z3(D[6]), .Z4(D[7]), .Y2(D[1]), .A3(T[2]),
    .A4(T[3]), .OEA(nE_MDR_HIGH), .B1(T[4]), .A1(T[0]), .B2(T[5]), .B3(T[6]), .B4(T[7]), .OEB(nE_MDR_HIGH),
    .A2(T[1]));
  IC_74244 ic_74244_2 (
    .Y3(D[2]), .Y4(D[3]), .Z1(D[4]), .Y1(D[0]), .Z2(D[5]), .Z3(D[6]), .Z4(D[7]), .Y2(D[1]), .A3(T[10]),
    .A4(T[11]), .OEA(nE_MDR_LOW), .B1(T[12]), .A1(T[8]), .B2(T[13]), .B3(T[14]), .B4(T[15]),
    .OEB(nE_MDR_LOW), .A2(T[9]));
  assign L = not_3_out ? T : 16'bz;  // Controlled_Buffer U59_60
  not not_3 (not_3_out, nEL_MDR);
  assign R = not_4_out ? T : 16'bz;  // Controlled_Buffer U57_58
  not not_4 (not_4_out, nER_MDR);

  // Notes on the sheet:
  //   Unused inputs to GND
endmodule
