// Logisim project Microcode.circ as structural Verilog: 1 circuit, main circuit Microcode
module Microcode (
  input  CLK_M,
  input  nFP_WRITE,
  input  nRESET,
  input  nDMA_ACQ,
  input  [3:0] ENCODER,
  input  [7:0] DBUS,
  input  INIT_INST,
  input  MSWC,
  input  MSWZ,
  input  FAULT_PENDING,
  input  MSWS,
  input  nDO_BRANCH,
  input  MSWV,
  output [3:0] LATCH,
  output XL_MAR,
  output R_RW,
  output XL_MDR_LO,
  output XL_MDR_HI,
  output nE_MDR_LO,
  output PRIV,
  output XL_MODE,
  output nE_MDR_HI,
  output XL_PAGING,
  output [3:0] MISC,
  output [3:0] EL,
  output [1:0] ER,
  output [1:0] RIMM_VAL,
  output [7:0] IR,
  output ALUOP_SZ,
  output [1:0] ALU_OP,
  output USE_CARRY,
  output LATCH_SZ,
  output RUSER_PTB,
  output CODE_PTB,
  output nNEXT0
);

  wire NEGATE_BR, not_1_out, U11_y, U12A_out, U12B_out, U13A_out, U13B_out, U13C_out, U14A_out, U14D_out,
       U14E_out, U21_out, U24_out, U61B_out;
  wire [7:0] NEXT_INST;
  wire [8:0] U61D_out;
  wire [16:15] register_1_q;
  wire [39:0] rom_1_data;

  not U14E (U14E_out, MSWC);
  xor U12B (U12B_out, MSWS, MSWV);
  IC_74273 ic_74273_1 (
    .Y2(IR[1]), .Y3(IR[2]), .Y1(IR[0]), .Y4(IR[3]), .Y5(IR[4]), .Y6(IR[5]), .Y7(IR[6]), .Y8(IR[7]),
    .D2(DBUS[1]), .D3(DBUS[2]), .D1(DBUS[0]), .D4(DBUS[3]), .D5(DBUS[4]), .D6(DBUS[5]), .D7(DBUS[6]),
    .D8(DBUS[7]), .CLK(INIT_INST), .CLR(nRESET));
  or U13C (U13C_out, U14E_out, MSWZ);
  or U13B (U13B_out, U12B_out, MSWZ);
  not U14A (U14A_out, MSWZ);
  IC_74151 U11 (
    .Y(U11_y), .C(U12B_out), .D(U13B_out), .E(U14E_out), .A(MSWZ), .F(U13C_out), .G(MSWZ), .J(U14A_out),
    .S0(IR[3]), .S1(IR[2]), .S2(IR[1]), .OE(1'b0), .B(MSWZ));  // open: Z
  nand U24 (U24_out, NEXT_INST[0], NEXT_INST[1], NEXT_INST[2], NEXT_INST[3], NEXT_INST[4], NEXT_INST[5], NEXT_INST[6], NEXT_INST[7]);
  xor U12A (U12A_out, NEGATE_BR, U11_y);
  Multiplexer #(.enable("false"), .select(2), .width(8)) multiplexer_1 (
    .in0({4'b0000, ENCODER[0], ENCODER[1], ENCODER[2], ENCODER[3]}),
    .in1({IR[0], IR[1], IR[2], IR[3], IR[4], IR[5], IR[6], IR[7]}),
    .in2({4'b0000, ENCODER[0], ENCODER[1], ENCODER[2], ENCODER[3]}),
    .in3({NEXT_INST[0], NEXT_INST[1], NEXT_INST[2], NEXT_INST[3], NEXT_INST[4], NEXT_INST[5], NEXT_INST[6], NEXT_INST[7]}),
    .out(U61D_out[7:0]), .sel({U61D_out[8], nNEXT0}));
  or U61D (U61D_out[8], U24_out, FAULT_PENDING);
  not U14D (U14D_out, FAULT_PENDING);
  or U13A (U13A_out, nDO_BRANCH, U12A_out);
  or U21 (U21_out, NEXT_INST[0], NEXT_INST[1], NEXT_INST[2], NEXT_INST[3], NEXT_INST[4], NEXT_INST[5], NEXT_INST[6], NEXT_INST[7]);
  and U44B (nNEXT0, U14D_out, U13A_out, U21_out);
  ROM #(.addrWidth(9), .dataWidth(40)) rom_1 (.addr(U61D_out), .data(rom_1_data));
  Register #(.width(40)) register_1 (
    .D(rom_1_data), .en(1'b1), .clk(CLK_M),
    .Q({CODE_PTB, RUSER_PTB, NEGATE_BR, LATCH_SZ, USE_CARRY, ALU_OP[0], ALU_OP[1], ALUOP_SZ, RIMM_VAL[0], RIMM_VAL[1], ER[0], ER[1], EL[0], EL[1], EL[2], EL[3], MISC[0], MISC[1], MISC[2], MISC[3], XL_PAGING, XL_MODE, PRIV, register_1_q, XL_MDR_HI, XL_MDR_LO, XL_MAR, LATCH[0], LATCH[1], LATCH[2], LATCH[3], NEXT_INST[0], NEXT_INST[1], NEXT_INST[2], NEXT_INST[3], NEXT_INST[4], NEXT_INST[5], NEXT_INST[6], NEXT_INST[7]}),
    .clr(not_1_out));
  not not_1 (not_1_out, nRESET);
  not U14C (nE_MDR_LO, register_1_q[15]);
  or U61B (U61B_out, nFP_WRITE, nDMA_ACQ);
  not U14B (nE_MDR_HI, register_1_q[16]);
  nand U25A (R_RW, U61B_out, nE_MDR_HI, nE_MDR_LO);

  // Notes on the sheet:
  //   contents of rom_1 (hex, n*v repeats v):
  //   96d3201300 965300533e 12d2000836 12db000836 12d4000836 9653005341 12d6000836 12d7000836 965300532e
  //   7*2d5001039 965300533e 965300333c 965300533e 965300533e 9653005341 965300333f 9653005341 9653005341
  //   4*9653005345 4*9653005349 9653005313 9653005313 12d1000836 9653005313 9653003312 6d60010e8
  //   12d5000836 12d7000812 9653005318 9653005318 6d60010f2 9653005318 96530053bf 9653007317 c2d7021070
  //   12d7000817 9653005313 9653005313 92d6001300 9653005313 9653003312 6d60010e8 12d6000812 12d7000812
  //   9653005318 9653005318 96530033b9 9653005318 96530053bf 9653007317 12d6000817 12d7000817 965300531c
  //   965300531c 12d7000200 965300531c 965300331b 506600000 12d6000817 12d700081b 9653005321 9653005321
  //   12d60008d0 9653005321 96530053c1 9653007320 406600000 12d7000820 9653005313 9653005313 13d6000600
  //   9653005313 9653003312 6d60010e8 965300532d 12d7000812 9653005318 9653005318 12d60008d1 9653005318
  //   96530053bf 9653007317 965300532e 12d7000817 9653005313 9653005313 12d70008d3 9653005313 9653003312
  //   6d60010e8 0 12d7000812 9653005318 9653005318 12d60008cf 9653005318 96530053bf 9653007317 2d70010d6
  //   12d7000817 4*965300535a 4*965300535c 965300335e 965300335f 9653007361 9653007363 9653005360
  //   9653005362 12d6000859 12d7000859 9653005368 9653003342 12d300086b 9653005366 9653007367 9653003346
  //   96530033db 96530033db 12d1000600 965300532d 200a2 400000 965300332f 9653003331 9653005332 9653005334
  //   9653005325 9653005325 12d6000700 9653005325 9653003324 12d8000824 12d6000200 12d7000824 965300532a
  //   965300532a 12d7000600 965300532a 96530053c0 9653007329 12d8000829 12d7000829 9653005325 9653005325
  //   12d70008ce 9653005325 9653003324 12d8000824 965300532d 12d7000824 965300532a 965300532a 12d70008cd
  //   965300532a 96530053c0 9653007329 965300532e 12d7000829 9653005325 9653005325 13d7000700 9653005325
  //   9653003324 965300532d 12d6000400 12d7000824 965300532a 965300532a 6d60010f2 965300532a 96530053c0
  //   9653007329 965300532e 12d7000829 965300532e 965300534d 12d60008be 12d6800600 12d70008bd 9653005354
  //   12d7800700 12d7000817 12d6020900 9653005351 200d5 12d6000500 6d60010e8 9653005357 9653005364
  //   965300532d 965300534d 965300334a 965300534d 965300534d 9653005354 9653003352 9653005354 9653005354
  //   9653005351 965300334e 9653005351 9653005351 9653005357 9653003355 9653005357 9653005357 82d70010bb
  //   12d4000600 9653007365 4970010dc 9653005371 6d8000871 12d60008c3 12d70008c3 412600077 41262007a
  //   412620081 2d700106e 42d70210bc 12d7000858 12d60008c8 12d70008c8 9653005325 9653005325 12d2000600
  //   9653005325 9653003324 12d8000824 12d5000600 12d7000824 965300532a 965300532a 3000fe 965300532a
  //   96530053c0 9653007329 12d8000829 12d7000829 96507033ff 6*2d0d00085 900000 2d0d00085 0 5*12d0000385 0
  //   60f001011 82d3003012 106600600 9653003310 60f001015 650005016 82d3003017 1006600600 9653003314
  //   60f00101a 82d300301b 506600000 9653003319 60f00101e 65000501f 82d3003020 406600000 965300331d
  //   60f001023 82d3003024 50660002b 9653003322 60f001027 650005028 82d3003029 40660002b 9653003326
  //   9653b0732c 9603001300 9653b0332c b653b0332c 306600030 b653b0732c 30660002b 9653003333 206600030
  //   9653003335 20660002b 6d5001037 16d0009538 82d3011000 65000503a 165000353b 12d8000fc2 60f00103d
  //   82d300305e 965300333c 60f001040 82d300305f 965300333f 60f001043 650005044 82d3003061 9653003342
  //   60f001047 650005048 82d3003063 9653003346 60f00104b 12d600084c 82d3009000 965300334a 60f00104f
  //   12d6000850 65001104c 965300334e 60f001053 12d700084c 9653003352 60f001056 12d7000850 9653003355
  //   1c06600600 1e06600600 965300335b 160f000600 965300335d 160f000700 2d8000600 2d8000700 9653003361
  //   12d8000600 9653003363 12d8000700 9653003365 12d8000200 9653003367 9603001300 9653003369 160300036a
  //   1403000836 6d500106c 16d000956d 92d6011300 206f 2d8000638 65000c2 9653003372 605001073 12d5000874
  //   6d0001075 16d0009576 12d00105c2 2000b00078 2d7001079 2d600307d 2000b2007b 42d700107c 2d600307d
  //   165000867e 165700077f 16d2000280 96d3001300 2000b20082 2d7001083 42d6003084 165000867e 12d1000886
  //   218a40087 6da001088 6d0009089 6d001108a 12d500088b 6d000908c 6d001108d 12db00088e 6d000908f
  //   6d0011090 12d600089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
endmodule
