// Logisim project PAGE_TABLE.circ as structural Verilog: 1 circuit, main circuit PAGE_TABLE
module PAGE_TABLE (
  input  [15:0] MAR,
  input  nRESET,
  input  L_PTB,
  input  [15:0] L_BUS,
  input  nL_PTE,
  input  nE_PTE,
  input  MSWM,
  input  MSWP,
  input  USER_PTB,
  input  CODE_PTB,
  input  L_MAR,
  input  nRW,
  input  XINIT_INST,
  input  XL_MDR_LO,
  input  XL_MDR_HI,
  input  nE_MDR_LO,
  input  nE_MDR_HI,
  input  CLKM,
  input  nDMA_ACK,
  output [15:0] T,
  output xMSWM,
  output xUSER_PTB,
  output nWAIT,
  output xMSWP,
  output MEMREF,
  output nNW,
  output xCODE_PTB,
  output nNP,
  output [21:0] A_BUS,
  output F,
  output M,
  output W,
  output P,
  output MEMORY
);

  wire not_1_out, not_2_out, U3_y3, U7_y1, U7_y2, U7_y3, U7_y4, U8_y1, U8_y2, U8_y3, U8_y4, U9_y1, U9_y2,
       U9_y3, U9_y4, U10_y1, U10_y2, U10_y3, U10_y4, U11A_out, U11C_out, U11D_out, U12_y1, U12_y2, U12_y3,
       U12_y4, U12_y5, U12_y6, U12_y7, U12_y8, U16A_out, U16C_out, U17A_out, U19B_out, U30B_out, U31_y5,
       U31_y6, U31_y7, U31_y8;
  wire [13:6] U15A_out;

  not not_1 (not_1_out, nL_PTE);
  and U16A (U16A_out, xMSWP, U8_y2);
  and U16C (U16C_out, nRESET, CLKM);
  RAM #(.addrWidth(14), .dataWidth(16), .trigger("low")) ram_1 (
    .addr({U15A_out, xCODE_PTB, MAR[4:0]}), .we(not_1_out), .oe(nE_PTE), .din(T), .dout(T));
  not U11A (U11A_out, nDMA_ACK);
  IC_74273 U31 (
    .Y2(xMSWP), .Y3(xUSER_PTB), .Y1(xMSWM), .Y4(xCODE_PTB), .Y5(U31_y5), .Y6(U31_y6), .Y7(U31_y7),
    .Y8(U31_y8), .D2(MSWP), .D3(USER_PTB), .D1(MSWM), .D4(CODE_PTB), .D5(1'b0), .D6(1'b0), .D7(1'b0),
    .D8(1'b0), .CLK(L_MAR), .CLR(nRESET));
  // NoConnect on U31_y5
  // NoConnect on U31_y6
  // NoConnect on U31_y7
  // NoConnect on U31_y8
  IC_74157 U8 (
    .Y2(U8_y2), .Y3(U8_y3), .Y4(U8_y4), .Y1(U8_y1), .A2(1'b0), .B2(T[2]), .A3(1'b0), .B3(T[1]), .A4(1'b0),
    .A1(1'b0), .B4(T[0]), .S0(xMSWP), .OE(1'b0), .B1(T[3]));
  IC_74374 U3 (
    .Y2(A_BUS[0]), .Y3(U3_y3), .Y1(A_BUS[1]), .Y4(F), .Y5(M), .Y6(W), .Y7(P), .Y8(MEMORY), .D2(U9_y3),
    .D3(U9_y4), .D1(U9_y2), .D4(U8_y1), .D5(U8_y2), .D6(U8_y3), .D7(U8_y4), .D8(U16A_out), .CLK(U16C_out),
    .OE(U11A_out));
  // NoConnect on U3_y3
  and U15A (U15A_out[6], U12_y8, U30B_out);
  and U15B (U15A_out[7], U12_y7, U30B_out);
  and U15C (U15A_out[8], U12_y6, U30B_out);
  and U15D (U15A_out[9], U12_y5, U30B_out);
  and U14A (U15A_out[10], U12_y4, U30B_out);
  and U14B (U15A_out[11], U12_y3, U30B_out);
  and U14C (U15A_out[12], U12_y2, U30B_out);
  and U14D (U15A_out[13], U12_y1, U30B_out);
  nand U19A (nWAIT, U19B_out, MEMREF);
  nand U20A (nNW, MEMREF, xMSWP, U11C_out, nRW);
  nand U18B (nNP, MEMREF, xMSWP, U11D_out);
  IC_74157 U9 (
    .Y2(U9_y2), .Y3(U9_y3), .Y4(U9_y4), .Y1(U9_y1), .A2(1'b0), .B2(T[6]), .A3(1'b0), .B3(T[5]), .A4(1'b0),
    .A1(1'b0), .B4(T[4]), .S0(xMSWP), .OE(1'b0), .B1(T[7]));
  IC_74273 U12 (
    .Y2(U12_y2), .Y3(U12_y3), .Y1(U12_y1), .Y4(U12_y4), .Y5(U12_y5), .Y6(U12_y6), .Y7(U12_y7), .Y8(U12_y8),
    .D2(L_BUS[14]), .D3(L_BUS[13]), .D1(L_BUS[15]), .D4(L_BUS[12]), .D5(L_BUS[11]), .D6(L_BUS[10]),
    .D7(L_BUS[9]), .D8(L_BUS[8]), .CLK(L_PTB), .CLR(nRESET));
  or U30B (U30B_out, xMSWM, xUSER_PTB);
  nand U19B (U19B_out, F, xMSWP);
  nand U18C (MEMREF, U17A_out, nE_MDR_LO, nE_MDR_HI);
  not U11C (U11C_out, W);
  not U11D (U11D_out, P);
  nor U17A (U17A_out, XINIT_INST, XL_MDR_LO, XL_MDR_HI);
  IC_74157 U10 (
    .Y2(U10_y2), .Y3(U10_y3), .Y4(U10_y4), .Y1(U10_y1), .A2(1'b0), .B2(T[10]), .A3(1'b0), .B3(T[9]),
    .A4(1'b0), .A1(MAR[0]), .B4(T[8]), .S0(xMSWP), .OE(1'b0), .B1(T[11]));
  IC_74374 U4 (
    .Y2(A_BUS[8]), .Y3(A_BUS[7]), .Y1(A_BUS[9]), .Y4(A_BUS[6]), .Y5(A_BUS[5]), .Y6(A_BUS[4]), .Y7(A_BUS[3]),
    .Y8(A_BUS[2]), .D2(U7_y3), .D3(U7_y4), .D1(U7_y2), .D4(U10_y1), .D5(U10_y2), .D6(U10_y3), .D7(U10_y4),
    .D8(U9_y1), .CLK(U16C_out), .OE(U11A_out));
  assign T = not_2_out ? L_BUS : 16'bz;  // Controlled_Buffer U32_33
  not not_2 (not_2_out, nE_PTE);
  IC_74157 U7 (
    .Y2(U7_y2), .Y3(U7_y3), .Y4(U7_y4), .Y1(U7_y1), .A2(MAR[3]), .B2(T[14]), .A3(MAR[2]), .B3(T[13]),
    .A4(MAR[1]), .A1(MAR[4]), .B4(T[12]), .S0(xMSWP), .OE(1'b0), .B1(T[15]));
  IC_74374 U5 (
    .Y2(A_BUS[16]), .Y3(A_BUS[15]), .Y1(A_BUS[17]), .Y4(A_BUS[14]), .Y5(A_BUS[13]), .Y6(A_BUS[12]),
    .Y7(A_BUS[11]), .Y8(A_BUS[10]), .D2(MAR[10]), .D3(MAR[9]), .D1(MAR[11]), .D4(MAR[8]), .D5(MAR[7]),
    .D6(MAR[6]), .D7(MAR[5]), .D8(U7_y1), .CLK(U16C_out), .OE(U11A_out));
  IC_74374 U6 (
    .Y5(A_BUS[21]), .Y6(A_BUS[20]), .Y7(A_BUS[19]), .Y8(A_BUS[18]), .D2(1'b0), .D3(1'b0), .D1(1'b0),
    .D4(1'b0), .D5(MAR[15]), .D6(MAR[14]), .D7(MAR[13]), .D8(MAR[12]), .CLK(U16C_out), .OE(U11A_out));  // open: Y2, Y3, Y1, Y4

  // Other names for the same wires on the sheet: MAR_4_0[4:0] = MAR[4:0]; MAR_5_15[10:0] = MAR[15:5]
endmodule
