// Logisim project RAM_ROM.circ as structural Verilog: 1 circuit, main circuit RAM_ROM
module RAM_ROM (
  input  nWE,
  input  [21:0] A,
  input  nOE,
  input  FP_RAM,
  input  MEMORY,
  output [7:0] DBUS
);

  wire and_1_out, and_2_out, nand_1_out, nand_2_out, nor_1_out, nor_2_out, nor_3_out, not_1_out, or_1_out;

  nor nor_1 (nor_1_out, A[6], A[5], A[4]);
  nor nor_2 (nor_2_out, A[3], A[2], A[1]);
  nor nor_3 (nor_3_out, A[0], MEMORY);
  and and_1 (and_1_out, nor_1_out, nor_2_out);
  or or_1 (or_1_out, A[7], FP_RAM);
  and and_2 (and_2_out, and_1_out, nor_3_out);
  RAM62256 ram62256_1 (
    .nWE(nWE),
    .A({A[7], A[8], A[9], A[10], A[11], A[12], A[13], A[14], A[15], A[16], A[17], A[18], A[19], A[20], A[21]}),
    .nOE(nOE), .nCS(nand_1_out), .D({DBUS[0], DBUS[1], DBUS[2], DBUS[3], DBUS[4], DBUS[5], DBUS[6], DBUS[7]}));
  ROM27256 rom27256_1 (
    .A({A[7], A[8], A[9], A[10], A[11], A[12], A[13], A[14], A[15], A[16], A[17], A[18], A[19], A[20], A[21]}),
    .nCS(nand_2_out), .nOE(nOE), .D({DBUS[0], DBUS[1], DBUS[2], DBUS[3], DBUS[4], DBUS[5], DBUS[6], DBUS[7]}));
  nand nand_1 (nand_1_out, and_2_out, or_1_out);
  nand nand_2 (nand_2_out, and_2_out, not_1_out);
  not not_1 (not_1_out, or_1_out);
endmodule
