// Logisim project REGS.circ as structural Verilog: 1 circuit, main circuit REGS
module REGS (
  input  [15:0] Z,
  input  [20:0] L_CTLBUS,
  input  [11:0] nEL_CTLBUS,
  input  [7:0] D_IN,
  input  [6:0] XL_CTLBUS,
  input  [1:0] nER_CTLBUS,
  input  nRESET,
  input  [1:0] IMMVAL,
  output [15:0] L,
  output [7:0] D_OUT,
  output [15:0] R,
  output [15:0] MAR
);

  GREGS gregs_1 (
    .L(L), .Z(Z), .L_SP(L_CTLBUS[14]), .nEL_SSP(nEL_CTLBUS[3]), .L_SSP(L_CTLBUS[10]), .nEL_PC(nEL_CTLBUS[6]),
    .L_PC(L_CTLBUS[12]), .L_A_HI(L_CTLBUS[8]), .nEL_TPC(nEL_CTLBUS[5]), .COMMIT(L_CTLBUS[5]),
    .n_EL_A(nEL_CTLBUS[7]), .L_A_LO(L_CTLBUS[15]), .L_B_HI(L_CTLBUS[9]), .n_EL_B(nEL_CTLBUS[8]),
    .L_B_LO(L_CTLBUS[16]), .nEL_C(nEL_CTLBUS[4]), .L_C(L_CTLBUS[11]), .nEL_DP(nEL_CTLBUS[9]),
    .L_DP(L_CTLBUS[13]), .nEL_SP(nEL_CTLBUS[10]), .nRESET(nRESET));
  MDR mdr_1 (
    .D_OUT(D_OUT), .L(L), .R(R), .nE_MDR_LO(XL_CTLBUS[6]), .nE_MDR_HI(XL_CTLBUS[5]), .nEL_MDR(nEL_CTLBUS[1]),
    .nER_MDR(nER_CTLBUS[1]), .D_IN(D_IN), .Z(Z), .L_MDR_LO(L_CTLBUS[2]), .COMMIT(L_CTLBUS[5]),
    .L_MDR_HI(L_CTLBUS[3]), .XL_MDR_LO(XL_CTLBUS[1]), .XL_MDR_HI(XL_CTLBUS[2]));  // open: out_15
  SREGS sregs_1 (
    .L_MAR(L_CTLBUS[4]), .Z(Z), .nRESET(nRESET), .nEL_MAR(nEL_CTLBUS[0]), .IMMVAL(IMMVAL),
    .nER_IMM(nER_CTLBUS[0]), .MAR(MAR), .L(L), .R(R));
endmodule
